# Fritzing sketch table top robot schematic (saved by Fritzing 0.9.10b)
breadboards: 1

parts:
  LED1 = LED - 5mm [color="White (4500K)" current=0.030 package="5 mm [THT]"]
  R1 = Resistor [tolerance=±5% power=0.25 resistance=220 package=THT]
  R2 = Resistor [tolerance=±5% power=0.25 resistance=220 package=THT]
  R3 = Resistor [tolerance=±5% power=0.25 resistance=220 package=THT]
  R4 = Resistor [tolerance=±5% power=0.25 resistance=220 package=THT]
  LED2 = LED - 5mm [color="Yellow (595nm)" current=0.030 package="5 mm [THT]"]
  VCC1 = Battery
  LED3 = LED - 5mm [color="Yellow (595nm)" current=0.030 package="5 mm [THT]"]
  LED4 = LED - 5mm [color="White (4500K)" current=0.030 package="5 mm [THT]"]
  Part2 = Arduino Uno (Rev3) - ICSP  # not connected
  Mod1 = Arduino Sensor Shield v5.0
  J1 = Power Jack [package=power_jack_slot]
  U1 = SWITCH-SPST-2 [package=switch-spst-vertical]
  HC-SR04_Sensor_1 = HC-SR04 Ultrasonic Distance Sensor
  M1 = fc-51 [package=THT]
  M2 = fc-51 [package=THT]
  M3 = fc-51 [package=THT]
  S1 = H-Bridge with L298N
  M4 = gear-motor
  M5 = gear-motor

nets:
  GND: LED1.cathode, LED2.cathode, LED3.cathode, LED4.cathode, Mod1.GND, Mod1.A0-GND, Mod1.A3-GND, Mod1.A5-GND, Mod1.BLUETOOTH-GND, Mod1.GND-S, Mod1.GND-G, HC-SR04_Sensor_1.GND, M1.pin2, M2.pin2, M3.pin1
  N1: LED1.anode, R1.Pin_0
  N2: R1.Pin_1, Mod1.2-S, Mod1.SerialLCD-D2
  N3: R2.Pin_0, LED2.anode
  N4: R2.Pin_1, Mod1.3-S, Mod1.SerialLCD-D3
  N5: R3.Pin_0, LED3.anode
  N6: R3.Pin_1, Mod1.4-S, Mod1.SerialLCD-D4
  N7: R4.Pin_0, LED4.anode
  N8: R4.Pin_1, Mod1.5-S, Mod1.ParallelLCD-D5
  GND_2: VCC1.-, J1.GND, U1.O, S1.GND
  N9: VCC1.+, J1.GNDBREAK, U1.P, S1.12V
  VCC: Mod1.VCC, Mod1.URF01-VCC, Mod1.A0-VCC, Mod1.A2-VCC, Mod1.A3-VCC, Mod1.A5-VCC, HC-SR04_Sensor_1.VCC, M1.pin3, M2.pin1, M3.pin3
  N10: Mod1.SD-D11, Mod1.11-S, S1.ENA
  N11: Mod1.SD-D13, Mod1.13-S, HC-SR04_Sensor_1.TRIG
  N12: Mod1.SD-D12, Mod1.12-S, HC-SR04_Sensor_1.ECHO
  N13: Mod1.URF01-A0, Mod1.A0-SIG, M1.pin1
  N14: Mod1.A3-SIG, M3.pin2
  N15: Mod1.A5-SIG, M2.pin3
  N16: Mod1.10-S, Mod1.ParallelLCD-D10, S1.IN1
  N17: Mod1.9-S, Mod1.ParallelLCD-D9, S1.IN2
  N18: Mod1.8-S, Mod1.ParallelLCD-D8, S1.IN3
  N19: Mod1.7-S, Mod1.ParallelLCD-D7, S1.IN4
  N20: Mod1.6-S, Mod1.ParallelLCD-D6, S1.ENB
  N21: S1.M1-01, M4.pin_2
  N22: S1.M1-02, M4.pin_1
  N23: S1.M2-01, M5.pin_1
  N24: S1.M2-02, M5.pin_2

custom parts:
  H-Bridge with L298N: h-bridge
